// Logisim project procesor.circ as structural Verilog
module Procesor (
  input  [15:0] in_1,
  input  LD,
  input  [15:0] in_3,
  output [15:0] out_4,
  output [7:0] out_5,
  output [7:0] out_6,
  output [7:0] out_7
);

  wire clk, main_1_p3, main_1_p4, main_1_p5, main_1_p7, main_1_p8, main_1_p9, not_1_out;
  wire [3:0] main_1_p6;
  wire [7:0] MEM, registers_1_p9, registers_1_p10;

  Clock u_CLK (.out(clk));
  // CU_main main_1: pin names not known; wires that end beside it: in_3, MEM, main_1_p3, main_1_p4, main_1_p5, main_1_p6, main_1_p7, main_1_p8, main_1_p9
  not not_1 (not_1_out, main_1_p5);
  RAM #(.dataWidth(16), .bus("separate")) ram_1 (
    .din(in_1), .data(out_4), .clk(clk), .ld(LD));  // open: addr, str, sel, clr
  // Registers registers_1: pin names not known; wires that end beside it: out_7, main_1_p7, main_1_p9, main_1_p8, clk, main_1_p3, not_1_out, out_6, registers_1_p9, registers_1_p10
  RAM #(.bus("separate")) ram_2 (
    .addr(MEM), .din(out_6), .data(out_7), .str(main_1_p5), .clk(clk), .ld(not_1_out));  // open: sel, clr
  ALU alu_1 (
    .R1__Value_of_first_register(registers_1_p9), .R2__Value_of_second_register(registers_1_p10),
    .OUT__ALU_output(out_5), .COM__Value_of_command__0000_to_1111(main_1_p6));  // open: FLAGS_ZCOP

  // Other names for the same wires on the sheet: AX[7:0] = out_6

  // Notes on the sheet:
  //   INSTRUCTIONS
  //   DATA
endmodule
